// Logisim project main.circ as structural Verilog: 2 circuits, main circuit main
module main (
  input  in_1,
  output out_2,
  output [7:0] out_3
);

  wire clock_1_out;
  wire [7:0] rom_1_data;
  wire [11:0] consoler_1_mem_a;

  Clock clock_1 (.out(clock_1_out));
  consoler consoler_1 (
    .CLK(clock_1_out), .RESET(in_1), .IT_WORKED(out_2), .INPUT_CHAR(out_3), .PRINT_SIZE(12'had5),
    .MEM_A(consoler_1_mem_a), .MEM_D(rom_1_data));
  ROM #(.addrWidth(12)) rom_1 (.addr(consoler_1_mem_a), .data(rom_1_data));  // open: sel

  // Notes on the sheet:
  //   contents of rom_1 (hex, n*v repeats v):
  //   0 76*23 a 23 52*20 23 21*20 23 a 23 52*20 23 21*20 23 a 23 52*20 23 21*20 23 a 23 52*20 23 21*20 23
  //   a 23 52*20 23 21*20 23 a 23 52*20 23 21*20 23 a 23 52*20 23 21*20 23 a 23 52*20 23 21*20 23 a 23
  //   52*20 23 21*20 23 a 23 52*20 23 21*20 23 a 23 52*20 23 21*20 23 a 23 52*20 23 21*20 23 a 23 52*20 23
  //   21*20 23 a 23 52*20 23 21*20 23 a 23 52*20 23 21*20 23 a 23 52*20 23 21*20 23 a 23 52*20 23 21*20 23
  //   a 23 52*20 23 21*20 23 a 23 52*20 23 21*20 23 a 23 52*20 23 21*20 23 a 23 52*20 23 21*20 23 a 23
  //   52*20 23*23 a 23 52*20 23 21*20 23 a 23 52*20 23 21*20 23 a 23 52*20 23 21*20 23 a 23 52*20 23 21*20
  //   23 a 23 52*20 23 21*20 23 a 76*23 a 23 74*20 23 a 76*23 a 23 9*20 23 9*20 23 9*20 23 9*20 23 9*20 23
  //   20 48 50 20 7c 10*20 7c 28 20 20 2f 31 30 29 20 23 a 23 9*20 23 9*20 23 9*20 23 9*20 23 9*20 23 20
  //   53 54 20 7c 10*20 7c 28 20 20 2f 31 30 29 20 23 a 23 9*20 23 9*20 23 9*20 23 9*20 23 9*20 23 20 48
  //   47 20 7c 10*20 7c 28 20 20 2f 31 30 29 20 23 a 23 9*20 23 9*20 23 9*20 23 9*20 23 9*20 23 24*20 23 a
  //   76*23 a
endmodule

module consoler (
  input  CLK,
  input  [7:0] MEM_D,
  input  [11:0] PRINT_SIZE,
  input  RESET,
  output IT_WORKED,
  output [7:0] INPUT_CHAR,
  output [11:0] MEM_A
);

  wire adder_1_out, and_3_out, and_4_out, clc, comparator_2_eq, not_1_out, not_2_out, not_3_out, not_4_out,
       not_5_out, or_2_out, PRND, readConsole, register_1_q, register_2_q, RES, RESET_MEMORY_COUNTER_out,
       uart_1_p3, uart_1_p6, uart_1_p8;
  wire [7:0] uart_1_p1;
  wire [11:0] adder_2_out;

  not not_1 (not_1_out, RESET);
  Register #(.width(1)) register_1 (.D(RESET), .Q(register_1_q), .clk(RESET), .clr(not_2_out));  // open: en
  not not_2 (not_2_out, not_1_out);
  and and_1 (clc, CLK, not_3_out);
  not not_3 (not_3_out, RES);
  or or_1 (RES, register_1_q, RESET_MEMORY_COUNTER_out);
  Button RESET_MEMORY_COUNTER (.out(RESET_MEMORY_COUNTER_out));
  and and_2 (IT_WORKED, not_5_out, PRND, register_2_q);
  Register #(.width(1)) register_2 (.D(adder_1_out), .Q(register_2_q), .clk(or_2_out));  // open: en, clr
  or or_2 (or_2_out, RES, uart_1_p3);
  not not_4 (not_4_out, PRND);
  not not_5 (not_5_out, uart_1_p3);
  Adder #(.width(1)) adder_1 (.a(register_2_q), .b(1'b1), .out(adder_1_out));  // open: cin, cout
  Register #(.width(12)) register_3 (.D(adder_2_out), .Q(MEM_A), .clk(and_3_out), .clr(RES));  // open: en
  not not_6 (readConsole, PRND);
  and and_3 (and_3_out, not_4_out, clc);
  Adder #(.width(12)) adder_2 (.a(MEM_A), .b(12'h1), .out(adder_2_out));  // open: cin, cout
  Register register_4 (.D(uart_1_p1), .Q(INPUT_CHAR), .clk(and_4_out), .clr(RES));  // open: en
  and and_4 (and_4_out, clc, comparator_2_eq);
  Comparator #(.width(12)) comparator_1 (.a(MEM_A), .b(PRINT_SIZE), .eq(PRND));  // open: gt, lt
  Comparator comparator_2 (.a(INPUT_CHAR), .b({8{1'b0}}), .eq(comparator_2_eq));  // open: gt, lt
  // UART uart_1: pin names not known; wires that end beside it: uart_1_p1, MEM_D, uart_1_p3, clc, uart_1_p3, uart_1_p6, uart_1_p6, uart_1_p8
  or or_3 (uart_1_p8, uart_1_p3, readConsole);

  // Notes on the sheet:
  //   Frame Printed
  //   Print Frame
  //   Input writened
  //   12 бит адрес
endmodule
